# Fritzing sketch Proyecto_001__Apaga_enciende_Led (saved by Fritzing 0.9.3b)
breadboards: 1

parts:
  Componente2 = Arduino Mega 2560 (Rev3)
  LED1 = LED - 5mm [color="Red (633nm)" package="5 mm [THT]"]
  R1 = Resistor [tolerance=±5% resistance=360 package=THT]

nets:
  N1: Componente2.GND, R1.Pin_0
  N2: Componente2.D13_PWM, LED1.anode
  N3: LED1.cathode, R1.Pin_1
