# Fritzing sketch Proyecto_002__HC_SR1_Sensor_proximidad (saved by Fritzing 0.9.3b)
breadboards: 1

parts:
  Componente1 = Arduino Mega 2560 (Rev3)
  hc-sr1 = hc-sr04
  LED1 = LED - 5mm [color="Red (633nm)" package="5 mm [THT]"]
  R1 = Resistor [tolerance=±5% resistance=360 package=THT]

nets:
  N1: Componente1.D13_PWM, hc-sr1.Trig
  N2: Componente1.D12_PWM, hc-sr1.Echo
  5V: Componente1.5V, hc-sr1.VCC
  GND: Componente1.GND, hc-sr1.GND, R1.Pin_1
  N3: Componente1.D2_PWM, LED1.anode
  N4: LED1.cathode, R1.Pin_0
