# Fritzing sketch Proyecto_003__Sensor_proximidad_barra_led (saved by Fritzing 0.9.3b)
breadboards: 1

parts:
  Componente1 = Arduino Mega 2560 (Rev3)
  hc-sr1 = hc-sr04
  LED1 = LED - 5mm [color="Red (633nm)" package="5 mm [THT]"]
  R1 = Resistor [tolerance=±5% resistance=360 package=THT]
  R2 = Resistor [tolerance=±5% resistance=360 package=THT]
  LED2 = LED - 5mm [color="Red (633nm)" package="5 mm [THT]"]
  LED3 = LED - 5mm [color="Red (633nm)" package="5 mm [THT]"]
  LED4 = LED - 5mm [color="Red (633nm)" package="5 mm [THT]"]
  LED5 = LED - 5mm [color="Red (633nm)" package="5 mm [THT]"]
  R3 = Resistor [tolerance=±5% resistance=360 package=THT]
  R4 = Resistor [tolerance=±5% resistance=360 package=THT]
  R5 = Resistor [tolerance=±5% resistance=360 package=THT]

nets:
  N1: Componente1.D13_PWM, hc-sr1.Trig
  N2: Componente1.D12_PWM, hc-sr1.Echo
  5V: Componente1.5V, hc-sr1.VCC
  GND: Componente1.GND, hc-sr1.GND, R1.Pin_1, R2.Pin_1, R3.Pin_1, R4.Pin_1, R5.Pin_1
  N3: Componente1.D0_RX0, LED1.anode
  N4: Componente1.D1_TX0, LED2.anode
  N5: Componente1.D2_PWM, LED3.anode
  N6: Componente1.D3_PWM, LED4.anode
  N7: Componente1.D4_PWM, LED5.anode
  N8: LED1.cathode, R1.Pin_0
  N9: R2.Pin_0, LED2.cathode
  N10: LED3.cathode, R3.Pin_0
  N11: LED4.cathode, R4.Pin_0
  N12: LED5.cathode, R5.Pin_0
