# Fritzing sketch Proyecto_005__Potenciometro (saved by Fritzing 0.9.3b)
breadboards: 1

parts:
  Componente1 = Arduino Mega 2560 (Rev3)
  LCD1 = LCD screen
  S1 = Pushbutton [package="[SMD]"]
  RE1 = Rotary Encoder [package=THT]
  R1 = Resistor [tolerance=±5% resistance=220 package=THT]

nets:
  N1: Componente1.A7, Componente1.5V, LCD1.LED-, S1.Pin_1, S1.Pin_2, RE1.EncoderPinA, RE1.EncoderPinC
  N2: Componente1.D20/SDA, LCD1.VSS
  N3: Componente1.D19/RX1, LCD1.VDD
  N4: Componente1.GND, LCD1.LED+, RE1.EncoderPinB, R1.Pin_0
  N5: Componente1.D7_PWM, S1.Pin_3, S1.Pin_4, R1.Pin_1
